# Fritzing sketch Sluch Weekend 2024-02-27 (saved by Fritzing 1.0.0rc)
circuit board: 6cm x 4.6cm
perfboards: 1

parts:
  R1 = Resistor [tolerance=±5% power=0.25W resistance=1k package=THT]
  R2 = Resistor [tolerance=±5% power=0.25W resistance=1k package=THT]
  R3 = Resistor [tolerance=±5% power=0.25W resistance=390k package=THT]
  R4 = Resistor [tolerance=±5% power=0.25W resistance=390k package=THT]
  OPA2134PA = LM 358 Dual Op-Amp [package="DIP8 [THT]"]
  C6 = Electrolytic Capacitor [capacitance=0.1mF voltage=63V mn=100µF package="100 mil [THT, electrolytic]"]
  R5 = Resistor [tolerance=±5% power=0.25W resistance=100k package=THT]
  R6 = Resistor [tolerance=±5% power=0.25W resistance=100k package=THT]
  C5 = Electrolytic Capacitor [capacitance=0.1mF voltage=63V mn=100µF package="100 mil [THT, electrolytic]"]
  J1 = Screw terminal - 2 pins [package=THT]
  C1 = Electrolytic Capacitor [capacitance=2.2µF voltage=35V package="100 mil [THT, electrolytic]"]
  C2 = Electrolytic Capacitor [capacitance=2.2µF voltage=35V package="100 mil [THT, electrolytic]"]
  C3 = Electrolytic Capacitor [capacitance=2.2µF voltage=35V package="100 mil [THT, electrolytic]"]
  C4 = Electrolytic Capacitor [capacitance=2.2µF voltage=35V package="100 mil [THT, electrolytic]"]
  L1 = WE-TE Inductor [part_number=22mH package="200 mil [THT]"]
  L2 = WE-TE Inductor [part_number=22mH package="200 mil [THT]"]
  LED1 = LED - 5mm [color="Green (565nm)" current=20mA package="5 mm [THT]"]
  R7 = Resistor [tolerance=±5% power=0.25W resistance=360 package=THT]
  Audio = AUDIO-JACK2 [package=audio-jack]

nets:
  N1: R1.Pin_0, C1.+
  N2: R1.Pin_1, R3.Pin_1, OPA2134PA.connector1
  N3: R2.Pin_0, C2.+
  N4: R2.Pin_1, R4.Pin_1, OPA2134PA.connector5
  N5: R3.Pin_0, OPA2134PA.connector0, C3.+
  N6: R4.Pin_0, OPA2134PA.connector6, C4.+
  N7: OPA2134PA.connector2, OPA2134PA.connector4, C6.-, R5.Pin_1, R6.Pin_0, C5.+, L1.pin_1, L2.pin_0, Audio.SLEEVE
  N8: OPA2134PA.connector3, R5.Pin_0, C5.-, J1.pin2, LED1.cathode
  N9: OPA2134PA.connector7, C6.+, R6.Pin_1, J1.pin1, R7.Pin_1
  N10: C1.-, L1.pin_0
  N11: C2.-, L2.pin_1
  N12: C3.-, Audio.RING
  N13: C4.-, Audio.TIP
  N14: LED1.anode, R7.Pin_0

notes:
  +
  Elektrosluch
  v.2024-02-17
  .
  -
  by DM9GP
